// Digital circuit ALU.dig as structural Verilog
module ALU (
  input  [15:0] X,
  input  [15:0] Y,
  input  [1:0] OP,
  input  ZX,
  input  ZY,
  input  NO,
  output [15:0] O,
  output isNeg,
  output isZero
);

  ArithUnit arithunit_1 (.X(X), .Y(Y), .OP(OP), .ZX(ZX), .ZY(ZY), .NO(NO), .O(O));
  // PreJumpFlags prejumpflags_1: pin names not known; wires that end beside it: O, isNeg, isZero
endmodule
