// Digital circuit ArithUnit.dig as structural Verilog
module ArithUnit (
  input  [15:0] X,
  input  [15:0] Y,
  input  [1:0] OP,
  input  ZX,
  input  ZY,
  output [15:0] O
);

  wire [15:0] add_1_s, and_1_out, multiplexer_1_out, multiplexer_2_out, or_1_out, sub_1_s;

  Multiplexer #(.Bits(16)) multiplexer_1 (.sel(ZX), .in_0(X), .in_1({16{1'b0}}), .out(multiplexer_1_out));
  Multiplexer #(.Bits(16)) multiplexer_2 (.sel(ZY), .in_0(Y), .in_1({16{1'b0}}), .out(multiplexer_2_out));
  assign or_1_out = multiplexer_1_out | multiplexer_2_out;  // Or or_1, 16 bits wide
  assign and_1_out = multiplexer_1_out & multiplexer_2_out;  // And and_1, 16 bits wide
  Add #(.Bits(16)) add_1 (.a(multiplexer_1_out), .b(multiplexer_2_out), .c_i(1'b0), .s(add_1_s));  // open: c_o
  Sub #(.Bits(16)) sub_1 (.a(multiplexer_1_out), .b(multiplexer_2_out), .c_i(1'b0), .s(sub_1_s));  // open: c_o
  Multiplexer #(.Bits(16), .Selector_Bits(2)) multiplexer_3 (
    .sel(OP), .in_0(or_1_out), .in_1(and_1_out), .in_2(add_1_s), .in_3(sub_1_s), .out(O));
endmodule
