// Digital circuit RAM.dig as structural Verilog
module RAM (
  input  [15:0] A,
  input  [15:0] D,
  input  C,
  input  a_3,
  input  d_2,
  input  m,
  output [15:0] A_2,
  output [15:0] D_3,
  output [15:0] M_2
);

  wire [1:0] priorityencoder_1_num;
  wire [15:0] Addr_q, Data_q, reg8192_1_o;

  Register #(.Bits(16)) Addr (.D(D), .C(C), .en(a_3), .Q(Addr_q));
  Register #(.Bits(16)) Data (.D(D), .C(C), .en(d_2), .Q(Data_q));
  reg8192 reg8192_1 (.A(A[12:0]), .C(C), .D(D), .RW(m), .O(reg8192_1_o));
  PriorityEncoder #(.Selector_Bits(2)) priorityencoder_1 (
    .in0(a_3), .in1(d_2), .in2(m), .in3(1'b0), .num(priorityencoder_1_num));  // open: any
  Multiplexer #(.Selector_Bits(2), .Bits(16)) multiplexer_1 (
    .sel(priorityencoder_1_num), .in_0(Addr_q), .in_1(Data_q), .in_2(reg8192_1_o), .in_3({16{1'b0}}),
    .out(A_2));
endmodule
