// Digital circuit reg128.dig as structural Verilog
module reg128 (
  input  [6:0] A,
  input  C,
  input  [15:0] D,
  input  RW,
  output [15:0] O
);

  wire demultiplexer_1_out_0, demultiplexer_1_out_1, demultiplexer_1_out_2, demultiplexer_1_out_3;
  wire [15:0] reg32_v2_1_o, reg32_v2_2_o, reg32_v2_3_o, reg32_v2_4_o;

  Demultiplexer #(.Selector_Bits(2)) demultiplexer_1 (
    .sel(A[6:5]), .in(RW), .out_0(demultiplexer_1_out_0), .out_1(demultiplexer_1_out_1),
    .out_2(demultiplexer_1_out_2), .out_3(demultiplexer_1_out_3));
  reg32_v2 reg32_v2_1 (.A(A[4:0]), .C(C), .D(D), .RW(demultiplexer_1_out_0), .O(reg32_v2_1_o));
  reg32_v2 reg32_v2_2 (.A(A[4:0]), .C(C), .D(D), .RW(demultiplexer_1_out_1), .O(reg32_v2_2_o));
  reg32_v2 reg32_v2_3 (.A(A[4:0]), .C(C), .D(D), .RW(demultiplexer_1_out_2), .O(reg32_v2_3_o));
  reg32_v2 reg32_v2_4 (.A(A[4:0]), .C(C), .D(D), .RW(demultiplexer_1_out_3), .O(reg32_v2_4_o));
  Multiplexer #(.Selector_Bits(2), .Bits(16)) multiplexer_1 (
    .sel(A[6:5]), .in_0(reg32_v2_1_o), .in_1(reg32_v2_2_o), .in_2(reg32_v2_3_o), .in_3(reg32_v2_4_o), .out(O));
endmodule
