// Digital circuit reg16.dig as structural Verilog
module reg16 (
  input  [3:0] A,
  input  C,
  input  [15:0] D,
  input  RW,
  output [15:0] O
);

  wire demultiplexer_1_out_0, demultiplexer_1_out_1;
  wire [15:0] reg8_1_o, reg8_2_o;

  Demultiplexer demultiplexer_1 (.sel(A[3]), .in(RW), .out_0(demultiplexer_1_out_0), .out_1(demultiplexer_1_out_1));
  reg8 reg8_1 (.A(A[2:0]), .C(C), .D(D), .RW(demultiplexer_1_out_0), .O(reg8_1_o));
  reg8 reg8_2 (.A(A[2:0]), .C(C), .D(D), .RW(demultiplexer_1_out_1), .O(reg8_2_o));
  Multiplexer #(.Bits(16)) multiplexer_1 (.sel(A[3]), .in_0(reg8_1_o), .in_1(reg8_2_o), .out(O));
endmodule
