// Digital circuit reg2.dig as structural Verilog
module reg2 (
  input  A,
  input  C,
  input  [15:0] D,
  input  RW,
  output [15:0] O
);

  wire and_1_out, and_2_out, not_1_out;
  wire [15:0] register_1_q, register_2_q;

  and and_1 (and_1_out, not_1_out, RW);
  not not_1 (not_1_out, A);
  and and_2 (and_2_out, A, RW);
  Register #(.Bits(16)) register_1 (.D(D), .C(C), .en(and_1_out), .Q(register_1_q));
  Register #(.Bits(16)) register_2 (.D(D), .C(C), .en(and_2_out), .Q(register_2_q));
  Multiplexer #(.Bits(16)) multiplexer_1 (.sel(A), .in_0(register_1_q), .in_1(register_2_q), .out(O));
endmodule
