// Digital circuit reg2048.dig as structural Verilog
module reg2048 (
  input  [10:0] A,
  input  C,
  input  [15:0] D,
  input  RW,
  output [15:0] O
);

  wire demultiplexer_1_out_0, demultiplexer_1_out_1, demultiplexer_1_out_2, demultiplexer_1_out_3;
  wire [15:0] reg512_1_o, reg512_2_o, reg512_3_o, reg512_4_o;

  Demultiplexer #(.Selector_Bits(2)) demultiplexer_1 (
    .sel(A[10:9]), .in(RW), .out_0(demultiplexer_1_out_0), .out_1(demultiplexer_1_out_1),
    .out_2(demultiplexer_1_out_2), .out_3(demultiplexer_1_out_3));
  reg512 reg512_1 (.A(A[8:0]), .C(C), .D(D), .RW(demultiplexer_1_out_0), .O(reg512_1_o));
  reg512 reg512_2 (.A(A[8:0]), .C(C), .D(D), .RW(demultiplexer_1_out_1), .O(reg512_2_o));
  reg512 reg512_3 (.A(A[8:0]), .C(C), .D(D), .RW(demultiplexer_1_out_2), .O(reg512_3_o));
  reg512 reg512_4 (.A(A[8:0]), .C(C), .D(D), .RW(demultiplexer_1_out_3), .O(reg512_4_o));
  Multiplexer #(.Selector_Bits(2), .Bits(16)) multiplexer_1 (
    .sel(A[10:9]), .in_0(reg512_1_o), .in_1(reg512_2_o), .in_2(reg512_3_o), .in_3(reg512_4_o), .out(O));
endmodule
