// Digital circuit reg32.dig as structural Verilog
module reg32 (
  input  [4:0] A,
  input  C,
  input  D,
  input  RW,
  output O
);

  wire demultiplexer_1_out_0, demultiplexer_1_out_1, reg16_1_p5, reg16_2_p5;

  Demultiplexer demultiplexer_1 (.sel(A[4]), .in(RW), .out_0(demultiplexer_1_out_0), .out_1(demultiplexer_1_out_1));
  // reg16 reg16_1: pin names not known; wires that end beside it: A[3:0], C, D, demultiplexer_1_out_0, reg16_1_p5
  // reg16 reg16_2: pin names not known; wires that end beside it: A[3:0], C, D, demultiplexer_1_out_1, reg16_2_p5
  Multiplexer multiplexer_1 (.sel(A[4]), .in_0(reg16_1_p5), .in_1(reg16_2_p5), .out(O));
endmodule
