// Digital circuit reg32_v2.dig as structural Verilog
module reg32_v2 (
  input  [4:0] A,
  input  C,
  input  [15:0] D,
  input  RW,
  output [15:0] O
);

  wire demultiplexer_1_out_0, demultiplexer_1_out_1, demultiplexer_1_out_2, demultiplexer_1_out_3;
  wire [15:0] reg8_v2_1_o, reg8_v2_2_o, reg8_v2_3_o, reg8_v2_4_o;

  Demultiplexer #(.Selector_Bits(2)) demultiplexer_1 (
    .sel(A[4:3]), .in(RW), .out_0(demultiplexer_1_out_0), .out_1(demultiplexer_1_out_1),
    .out_2(demultiplexer_1_out_2), .out_3(demultiplexer_1_out_3));
  reg8_v2 reg8_v2_1 (.A(A[2:0]), .C(C), .D(D), .RW(demultiplexer_1_out_0), .O(reg8_v2_1_o));
  reg8_v2 reg8_v2_2 (.A(A[2:0]), .C(C), .D(D), .RW(demultiplexer_1_out_1), .O(reg8_v2_2_o));
  reg8_v2 reg8_v2_3 (.A(A[2:0]), .C(C), .D(D), .RW(demultiplexer_1_out_2), .O(reg8_v2_3_o));
  reg8_v2 reg8_v2_4 (.A(A[2:0]), .C(C), .D(D), .RW(demultiplexer_1_out_3), .O(reg8_v2_4_o));
  Multiplexer #(.Selector_Bits(2), .Bits(16)) multiplexer_1 (
    .sel(A[4:3]), .in_0(reg8_v2_1_o), .in_1(reg8_v2_2_o), .in_2(reg8_v2_3_o), .in_3(reg8_v2_4_o), .out(O));
endmodule
