// Digital circuit reg512.dig as structural Verilog
module reg512 (
  input  [8:0] A,
  input  C,
  input  [15:0] D,
  input  RW,
  output [15:0] O
);

  wire demultiplexer_1_out_0, demultiplexer_1_out_1, demultiplexer_1_out_2, demultiplexer_1_out_3;
  wire [15:0] reg128_1_o, reg128_2_o, reg128_3_o, reg128_4_o;

  Demultiplexer #(.Selector_Bits(2)) demultiplexer_1 (
    .sel(A[8:7]), .in(RW), .out_0(demultiplexer_1_out_0), .out_1(demultiplexer_1_out_1),
    .out_2(demultiplexer_1_out_2), .out_3(demultiplexer_1_out_3));
  reg128 reg128_1 (.A(A[6:0]), .C(C), .D(D), .RW(demultiplexer_1_out_0), .O(reg128_1_o));
  reg128 reg128_2 (.A(A[6:0]), .C(C), .D(D), .RW(demultiplexer_1_out_1), .O(reg128_2_o));
  reg128 reg128_3 (.A(A[6:0]), .C(C), .D(D), .RW(demultiplexer_1_out_2), .O(reg128_3_o));
  reg128 reg128_4 (.A(A[6:0]), .C(C), .D(D), .RW(demultiplexer_1_out_3), .O(reg128_4_o));
  Multiplexer #(.Selector_Bits(2), .Bits(16)) multiplexer_1 (
    .sel(A[8:7]), .in_0(reg128_1_o), .in_1(reg128_2_o), .in_2(reg128_3_o), .in_3(reg128_4_o), .out(O));
endmodule
