// Digital circuit reg64.dig as structural Verilog
module reg64 (
  input  [5:0] A,
  input  C,
  input  D,
  input  RW,
  output O
);

  wire demultiplexer_1_out_0, demultiplexer_1_out_1, reg32_1_o, reg32_2_o;

  Demultiplexer demultiplexer_1 (.sel(A[5]), .in(RW), .out_0(demultiplexer_1_out_0), .out_1(demultiplexer_1_out_1));
  reg32 reg32_1 (.A(A[4:0]), .C(C), .D(D), .RW(demultiplexer_1_out_0), .O(reg32_1_o));
  reg32 reg32_2 (.A(A[4:0]), .C(C), .D(D), .RW(demultiplexer_1_out_1), .O(reg32_2_o));
  Multiplexer multiplexer_1 (.sel(A[5]), .in_0(reg32_1_o), .in_1(reg32_2_o), .out(O));
endmodule
