// Digital circuit reg8.dig as structural Verilog
module reg8 (
  input  [2:0] A,
  input  C,
  input  [15:0] D,
  input  RW,
  output [15:0] O
);

  wire demultiplexer_1_out_0, demultiplexer_1_out_1;
  wire [15:0] reg4_1_o, reg4_2_o;

  Demultiplexer demultiplexer_1 (.sel(A[2]), .in(RW), .out_0(demultiplexer_1_out_0), .out_1(demultiplexer_1_out_1));
  reg4 reg4_1 (.A(A[1:0]), .C(C), .D(D), .RW(demultiplexer_1_out_0), .O(reg4_1_o));
  reg4 reg4_2 (.A(A[1:0]), .C(C), .D(D), .RW(demultiplexer_1_out_1), .O(reg4_2_o));
  Multiplexer #(.Bits(16)) multiplexer_1 (.sel(A[2]), .in_0(reg4_1_o), .in_1(reg4_2_o), .out(O));
endmodule
