// Digital circuit reg8192.dig as structural Verilog
module reg8192 (
  input  [12:0] A,
  input  C,
  input  [15:0] D,
  input  RW,
  output [15:0] O
);

  wire demultiplexer_1_out_0, demultiplexer_1_out_1, demultiplexer_1_out_2, demultiplexer_1_out_3;
  wire [15:0] reg2048_1_o, reg2048_2_o, reg2048_3_o, reg2048_4_o;

  Demultiplexer #(.Selector_Bits(2)) demultiplexer_1 (
    .sel(A[12:11]), .in(RW), .out_0(demultiplexer_1_out_0), .out_1(demultiplexer_1_out_1),
    .out_2(demultiplexer_1_out_2), .out_3(demultiplexer_1_out_3));
  reg2048 reg2048_1 (.A(A[10:0]), .C(C), .D(D), .RW(demultiplexer_1_out_0), .O(reg2048_1_o));
  reg2048 reg2048_2 (.A(A[10:0]), .C(C), .D(D), .RW(demultiplexer_1_out_1), .O(reg2048_2_o));
  reg2048 reg2048_3 (.A(A[10:0]), .C(C), .D(D), .RW(demultiplexer_1_out_2), .O(reg2048_3_o));
  reg2048 reg2048_4 (.A(A[10:0]), .C(C), .D(D), .RW(demultiplexer_1_out_3), .O(reg2048_4_o));
  Multiplexer #(.Selector_Bits(2), .Bits(16)) multiplexer_1 (
    .sel(A[12:11]), .in_0(reg2048_1_o), .in_1(reg2048_2_o), .in_2(reg2048_3_o), .in_3(reg2048_4_o), .out(O));
endmodule
