// Digital circuit computer.dig as structural Verilog
module computer (
  input  clk
);

  wire destA, destD, destM, instrType, isNeg, isZero, noFlg, setPC, zxFlg, zyFlg;
  wire [1:0] OP;
  wire [15:0] addrConst, aluOut, Areg, counterpreset_1_out, Dreg, I, Mreg, multiplexer_1_out,
       multiplexer_2_out, X, Y;

  Multiplexer #(.Bits(16)) multiplexer_1 (.sel(instrType), .in_0(aluOut), .in_1(addrConst), .out(multiplexer_1_out));
  CounterPreset #(.Bits(16)) counterpreset_1 (
    .en(1'b1), .C(clk), .dir(1'b0), .in(multiplexer_1_out), .ld(setPC), .clr(1'b0), .out(counterpreset_1_out));  // open: ovf
  ROM #(.AddrBits(16), .Bits(16)) PROG_MEM (.A(counterpreset_1_out), .sel(1'b1), .D(I));
  Multiplexer #(.Bits(16)) multiplexer_2 (.sel(instrType), .in_0(aluOut), .in_1(addrConst), .out(multiplexer_2_out));
  ALU alu_1 (.X(X), .Y(Y), .OP(OP), .ZX(zxFlg), .ZY(zyFlg), .NO(noFlg), .O(aluOut), .isNeg(isNeg), .isZero(isZero));
  control_unit control_unit_1 (
    .I(I), .Ain(Areg), .D(Dreg), .M(Mreg), .isNeg(isNeg), .isZero(isZero), .setPC(setPC), .Aout(addrConst),
    .OP(OP), .zx(zxFlg), .zy(zyFlg), .no(noFlg), .X(X), .Y(Y), .destA(destA), .destD(destD), .destM(destM),
    .instrType(instrType));
  RAM ram_1 (.Din(multiplexer_2_out), .C(clk), .a(destA), .d(destD), .m(destM), .Aout(Areg), .Dout(Dreg), .M_2(Mreg));

  // Notes on the sheet:
  //   clk: Hz: 1600
  //   contents of PROG_MEM (hex, n*v repeats v):
  //   800f,2040,2700,8000,7
endmodule
