// Digital circuit control_unit.dig as structural Verilog
module control_unit (
  input  [15:0] I,
  input  [15:0] Ain,
  input  [15:0] D,
  input  [15:0] M,
  input  isNeg,
  input  isZero,
  output setPC,
  output [15:0] Aout,
  output [1:0] OP,
  output zx,
  output zy,
  output no,
  output [15:0] X,
  output [15:0] Y,
  output destA,
  output destD,
  output destM,
  output instrType
);

  wire not_1_out, shouldjumpcheck_1_setpc;

  Multiplexer #(.Selector_Bits(2), .Bits(16)) multiplexer_1 (
    .sel(I[9:8]), .in_0(Ain), .in_1(D), .in_2(M), .in_3(16'h1), .out(X));
  Multiplexer #(.Selector_Bits(2), .Bits(16)) multiplexer_2 (
    .sel(I[11:10]), .in_0(Ain), .in_1(D), .in_2(M), .in_3(16'h1), .out(Y));
  or or_1 (destA, I[14], I[15]);
  shouldJumpCheck shouldjumpcheck_1 (.isNeg(isNeg), .isZero(isZero), .jmpCnd(I[2:0]), .setPC(shouldjumpcheck_1_setpc));
  not not_1 (not_1_out, I[15]);
  and and_1 (setPC, not_1_out, shouldjumpcheck_1_setpc);

  assign Aout = {1'b0, I[14:0]};
  assign destD = I[13];
  assign destM = I[12];
  assign instrType = I[15];
  assign no = I[5];
  assign OP = I[4:3];
  assign zx = I[7];
  assign zy = I[6];

  // Other names for the same wires on the sheet: jmpCnd[2:0] = I[2:0]; ops[1:0] = I[4:3]; flgs[2:0] = I[7:5];
  //   regSelects[3:0] = I[11:8]; destSelects[2:0] = I[14:12]
endmodule
