// Digital circuit PreJumpFlags.dig as structural Verilog
module PreJumpFlags (
  input  [15:0] Out,
  output isNeg,
  output isZero
);

  wire or_1_out;

  or or_1 (or_1_out, Out[0], Out[1], Out[2], Out[3], Out[4], Out[5], Out[6], Out[7], Out[8], Out[9], Out[10], Out[11], Out[12], Out[13], Out[14], Out[15]);
  not not_1 (isZero, or_1_out);
  // Pins of 1 and 16 bits meet at Out

  assign isNeg = Out[15];
endmodule
