// Digital circuit RAM.dig as structural Verilog
module RAM (
  input  [15:0] Din,
  input  C,
  input  a,
  input  d,
  input  m,
  output [15:0] Aout,
  output [15:0] Dout,
  output [15:0] M_2
);

  Register #(.Bits(16)) Addr (.D(Din), .C(C), .en(a), .Q(Aout));
  Register #(.Bits(16)) Data (.D(Din), .C(C), .en(d), .Q(Dout));
  reg8192 reg8192_1 (.A(Aout[12:0]), .C(C), .D(Din), .RW(m), .O(M_2));
endmodule
