// Digital circuit reg4.dig as structural Verilog
module reg4 (
  input  [1:0] A,
  input  C,
  input  [15:0] D,
  input  RW,
  output [15:0] O
);

  wire demultiplexer_1_out_0, demultiplexer_1_out_1;
  wire [15:0] reg2_1_o, reg2_2_o;

  Demultiplexer demultiplexer_1 (.sel(A[1]), .in(RW), .out_0(demultiplexer_1_out_0), .out_1(demultiplexer_1_out_1));
  reg2 reg2_1 (.A(A[0]), .C(C), .D(D), .RW(demultiplexer_1_out_0), .O(reg2_1_o));
  reg2 reg2_2 (.A(A[0]), .C(C), .D(D), .RW(demultiplexer_1_out_1), .O(reg2_2_o));
  Multiplexer #(.Bits(16)) multiplexer_1 (.sel(A[1]), .in_0(reg2_1_o), .in_1(reg2_2_o), .out(O));
endmodule
