// Digital circuit reg8_v2.dig as structural Verilog
module reg8_v2 (
  input  [2:0] A,
  input  C,
  input  [15:0] D,
  input  RW,
  output [15:0] O
);

  wire demultiplexer_1_out_0, demultiplexer_1_out_1, demultiplexer_1_out_2, demultiplexer_1_out_3;
  wire [15:0] reg2_1_o, reg2_2_o, reg2_3_o, reg2_4_o;

  Demultiplexer #(.Selector_Bits(2)) demultiplexer_1 (
    .sel(A[2:1]), .in(RW), .out_0(demultiplexer_1_out_0), .out_1(demultiplexer_1_out_1),
    .out_2(demultiplexer_1_out_2), .out_3(demultiplexer_1_out_3));
  reg2 reg2_1 (.A(A[0]), .C(C), .D(D), .RW(demultiplexer_1_out_0), .O(reg2_1_o));
  reg2 reg2_2 (.A(A[0]), .C(C), .D(D), .RW(demultiplexer_1_out_1), .O(reg2_2_o));
  reg2 reg2_3 (.A(A[0]), .C(C), .D(D), .RW(demultiplexer_1_out_2), .O(reg2_3_o));
  reg2 reg2_4 (.A(A[0]), .C(C), .D(D), .RW(demultiplexer_1_out_3), .O(reg2_4_o));
  Multiplexer #(.Bits(16), .Selector_Bits(2)) multiplexer_1 (
    .sel(A[2:1]), .in_0(reg2_1_o), .in_1(reg2_2_o), .in_2(reg2_3_o), .in_3(reg2_4_o), .out(O));
endmodule
