// Digital circuit shouldJumpCheck.dig as structural Verilog
module shouldJumpCheck (
  input  isNeg,
  input  isZero,
  input  [2:0] jmpCnd,
  output setPC
);

  wire and_1_out, and_2_out, and_3_out, and_4_out, and_5_out, and_6_out, and_7_out, decoder_1_out_0,
       decoder_1_out_1, decoder_1_out_2, decoder_1_out_3, decoder_1_out_4, decoder_1_out_5, decoder_1_out_6,
       decoder_1_out_7, not_1_out, not_2_out, or_1_out, or_2_out;

  Decoder #(.Selector_Bits(3)) decoder_1 (
    .sel(jmpCnd), .out_0(decoder_1_out_0), .out_1(decoder_1_out_1), .out_2(decoder_1_out_2),
    .out_3(decoder_1_out_3), .out_4(decoder_1_out_4), .out_5(decoder_1_out_5), .out_6(decoder_1_out_6),
    .out_7(decoder_1_out_7));
  not not_1 (not_1_out, isNeg);
  not not_2 (not_2_out, isZero);
  and and_1 (and_1_out, 1'b0, decoder_1_out_0);
  and and_2 (and_2_out, not_1_out, decoder_1_out_1);
  and and_3 (and_3_out, isZero, decoder_1_out_2);
  or or_1 (or_1_out, isZero, not_1_out);
  and and_4 (and_4_out, or_1_out, decoder_1_out_3);
  and and_5 (and_5_out, isNeg, decoder_1_out_4);
  and and_6 (and_6_out, not_2_out, decoder_1_out_5);
  or or_2 (or_2_out, isNeg, isZero);
  and and_7 (and_7_out, or_2_out, decoder_1_out_6);
  or or_3 (setPC, decoder_1_out_7, and_7_out, and_6_out, and_5_out, and_4_out, and_3_out, and_2_out, and_1_out);
endmodule
